# Fritzing sketch arduino-l293D-stepper (saved by Fritzing 0.8.5b)
breadboards: 1

parts:
  Part1 = Arduino Mega 2560 (Rev3)
  IC1 = L293D [package=THT]
  M1 = Stepper Motor - Bipolar

nets:
  N1: Part1.GND, IC1.0V
  N2: Part1.D9_PWM, IC1.In_4
  N3: Part1.3V3, IC1.+Vmotor, IC1.Enable_2, IC1.+V
  N4: Part1.D0_RX0, IC1.In_3
  N5: Part1.D1_TX0, IC1.In_2
  N6: Part1.D2_PWM, IC1.In_1
  N7: IC1.Out_1_(_Controlled_by_Enable_1_), M1.A
  N8: IC1.Out_2_(_Controlled_by_Enable_1_), M1.B
  N9: IC1.Out_3_(_Controlled_by_Enable_2_), M1.C
  N10: IC1.Out_4_(_Controlled_by_Enable_2_), M1.D
