# Fritzing sketch arduino-stepper-a4988 (saved by Fritzing 0.8.5b)
breadboards: 1

parts:
  M1 = Stepper Motor - Bipolar
  Part1 = Arduino Mega 2560 (Rev3)
  MD09B1 = A4988 Stepper Motor Driver Carrier
  VCC1 = Battery block 9V
  C1 = Electrolytic Capacitor [capacitance=100µF package="200 mil [THT, electrolytic]"]

nets:
  N1: M1.A, MD09B1.OUT_2B
  N2: M1.C, MD09B1.OUT_2A
  N3: M1.B, MD09B1.OUT_1A
  N4: M1.D, MD09B1.OUT_1B
  5V: Part1.5V, MD09B1.VDD
  N5: Part1.GND, MD09B1.GROUND#147
  N6: Part1.D4_PWM, MD09B1.DIR
  N7: Part1.D5_PWM, MD09B1.STEP
  N8: MD09B1.RESET, MD09B1.SLEEP
  N9: MD09B1.VMOT, VCC1.+, C1.+
  N10: MD09B1.GROUND#141, VCC1.-, C1.-
