# Fritzing sketch esp8266_simple (saved by Fritzing 0.8.5b)
circuit board: 2cm x 2.5cm
stripboards: 1

parts:
  J3 = single row smd male pin header, 4 pins [form="♂ (male)"]
  J4 = single row smd male pin header, 4 pins [form="♂ (male)"]
  J1 = female alternating pin header, 4 pins [form="♀ (female)"]
  J2 = female pin header, 4 pins [form="♀ (female)"]

nets:
  N1: J3.pin1, J2.pin1
  N2: J3.pin2, J2.pin2
  N3: J3.pin3, J2.pin3
  N4: J3.pin4, J2.pin4
  N5: J4.pin1, J1.pin1
  N6: J4.pin2, J1.pin2
  N7: J4.pin3, J1.pin3
  N8: J4.pin4, J1.pin4
