# Fritzing sketch raspberrypi-a4988-stepper (saved by Fritzing 0.8.5b)
breadboards: 1

parts:
  M1 = Stepper Motor - Bipolar
  MD09B1 = A4988 Stepper Motor Driver Carrier
  C1 = Electrolytic Capacitor [capacitance=100µF package="200 mil [THT, electrolytic]"]
  Pi1 = Adafruit Pi Cobbler
  Raspberry_Pi_B_rev1 = Raspberry Pi B rev2  # not connected
  BAT1 = BC9VPC [package=bc9vpc]

nets:
  N1: M1.A, MD09B1.OUT_2B
  N2: M1.C, MD09B1.OUT_2A
  N3: M1.B, MD09B1.OUT_1A
  N4: M1.D, MD09B1.OUT_1B
  N5: MD09B1.RESET, MD09B1.SLEEP
  N6: MD09B1.STEP, Pi1.#22
  N7: MD09B1.DIR, Pi1.#21
  N8: MD09B1.VMOT, C1.-, C1.+, BAT1.V+, BAT1.V-
  VDD: MD09B1.VDD, Pi1.3V3
  N9: MD09B1.GROUND#147, Pi1.GND

custom parts:
  Adafruit Pi Cobbler: Adafruit Pi Cobbler GPIO Breakout for Raspberry Pi
